// Logisim project 1.circ as structural Verilog: 1 circuit, main circuit main
module main (
  input  d,
  input  e,
  input  s,
  input  b,
  input  h,
  output x,
  output y,
  output z
);

  wire and_1_out, and_2_out, and_3_out, and_4_out, and_5_out, not_1_out, not_2_out, not_3_out, not_4_out,
       not_5_out;

  not not_1 (not_1_out, d);
  not not_2 (not_2_out, b);
  not not_3 (not_3_out, e);
  not not_4 (not_4_out, s);
  and and_1 (and_1_out, d, e);
  not not_5 (not_5_out, s);
  or or_1 (z, d, h);
  and and_2 (and_2_out, not_1_out, e);
  and and_3 (and_3_out, s, not_2_out, e);
  and and_4 (and_4_out, h, not_3_out);
  and and_5 (and_5_out, not_4_out, b, d);
  or or_2 (y, and_1_out, not_5_out);
  or or_3 (x, and_2_out, and_3_out, and_4_out, and_5_out);
endmodule
