// Logisim project 2.circ as structural Verilog: 1 circuit, main circuit main
module main (
  input  H,
  input  S,
  input  B,
  input  D,
  input  E,
  output out_6
);

  wire and_1_out, and_2_out, and_3_out, and_4_out, and_5_out, and_6_out, not_1_out, not_2_out, not_3_out,
       not_4_out, or_1_out, or_2_out;

  not not_1 (not_1_out, D);
  not not_2 (not_2_out, B);
  not not_3 (not_3_out, E);
  not not_4 (not_4_out, S);
  and and_1 (and_1_out, not_1_out, E);
  and and_2 (and_2_out, S, not_2_out);
  and and_3 (and_3_out, H, not_3_out);
  and and_4 (and_4_out, not_4_out, B);
  and and_5 (and_5_out, and_2_out, E);
  and and_6 (and_6_out, and_4_out, D);
  or or_1 (or_1_out, and_1_out, and_5_out);
  or or_2 (or_2_out, and_3_out, and_6_out);
  or or_3 (out_6, or_1_out, or_2_out);
endmodule
